// Logisim project SomadorCompleto.circ as structural Verilog: 2 circuits, main circuit main
module main (
);

  Meio_Somador meio_somador_1 ();  // open: Soma, Carry_Out, A0, B0
endmodule

module Meio_Somador (
  input  A0,
  input  B0,
  output Soma,
  output Carry_Out
);

  xor xor_1 (Soma, A0, B0);
  and and_1 (Carry_Out, A0, B0);
endmodule
